# Fritzing sketch PROJET Oxymètre Platine d'essai (saved by Fritzing 0.9.3b)
breadboards: 1

parts:
  LM324N1 = LM324N [package=dil14]
  Composant1 = Arduino Uno (Rev3)
  R1 = Resistor [tolerance=±5% resistance=22k package=THT]
  R2 = Resistor [tolerance=±5% resistance=2.2k package=THT]
  LED1 = LED - 5mm [color="Infrared (940nm)" package="5 mm [THT]"]
  IR1 = TSOP312.., 314.. [package=THT]
  R3 = Resistor [tolerance=±5% resistance=100 package=THT]
  LED2 = LED - 5mm [color="Red (633nm)" package="5 mm [THT]"]
  R4 = Resistor [tolerance=±5% resistance=470 package=THT]
  C1 = Ceramic Capacitor [capacitance=100nF package="200 mil [THT, multilayer]"]
  R5 = Resistor [tolerance=±5% resistance=1k package=THT]
  R6 = Resistor [tolerance=±5% resistance=220 package=THT]
  C2 = Ceramic Capacitor [capacitance=1µF package="200 mil [THT, multilayer]"]

nets:
  N1: LM324N1.Vcc_+, R1.Pin_0, R2.Pin_0
  N2: LM324N1.+_Non-inverting_Input_2, R6.Pin_0, C2.1
  N3: LM324N1.-_Inverting_Input_2, R4.Pin_1, C1.0, R5.Pin_0
  N4: LM324N1.Output_2, R3.Pin_1, R4.Pin_0, C1.1
  GND: LM324N1.Vcc_-, Composant1.GND, LED1.anode, IR1.GND, LED2.anode, R5.Pin_1
  N5: Composant1.A0, R3.Pin_0, LED2.cathode
  N6: R1.Pin_1, LED1.cathode
  N7: R2.Pin_1, IR1.Vs, C2.0

custom parts:
  LM324N: LM324 LOW POWER QUAD OPERATIONAL AMPLIFIERS
