# Fritzing sketch PROJET Oxymètre Schématique dernier (saved by Fritzing 0.9.3b)
circuit board: 8.46667cm x 5.64444cm
breadboards: 1

parts:
  LM324N1 = LM324N [package=dil14]
  Composant1 = Arduino Uno (Rev3)
  LED1 = LED - 5mm [color="Red (633nm)" package="5 mm [THT]"]
  C1 = Ceramic Capacitor [capacitance=1µF package="200 mil [THT, multilayer]"]
  C2 = Ceramic Capacitor [capacitance=100nF package="200 mil [THT, multilayer]"]
  C3 = Ceramic Capacitor [capacitance=100nF package="200 mil [THT, multilayer]"]
  C4 = Ceramic Capacitor [capacitance=1µF package="200 mil [THT, multilayer]"]
  IR1 = TSOP312.., 314.. [package=THT]
  LED2 = LED - 5mm [color="Infrared (940nm)" package="5 mm [THT]"]
  R1 = Resistor [tolerance=±5% resistance=68k package="1206 [SMD]"]
  R2 = Resistor [tolerance=±5% resistance=8.2k package="1206 [SMD]"]
  R3 = Resistor [tolerance=±5% resistance=68k package="1206 [SMD]"]
  R4 = Resistor [tolerance=±5% resistance=100 package="1206 [SMD]"]
  R5 = Resistor [tolerance=±5% resistance=22k package="1206 [SMD]"]
  R6 = Resistor [tolerance=±5% resistance=1k package="1206 [SMD]"]
  R7 = Resistor [tolerance=±5% resistance=470k package="1206 [SMD]"]

nets (from the schematic view):
  N1: LM324N1.output_1, C2.1, C4.0
  N2: LM324N1.-_Inverting_Input_1, C2.0, R2.Pin_1
  GND: LM324N1.+_Non-inverting_Input_1, LM324N1.Vcc_-, Composant1.GND, LED1.cathode, IR1.GND, LED2.cathode, R1.Pin_0, R2.Pin_0, R3.Pin_0
  N3: LM324N1.Vcc_+, Composant1.5V, IR1.Vs, R5.Pin_1, R6.Pin_1
  N4: LM324N1.+_Non-inverting_Input_4, C4.1, R3.Pin_1
  N5: LM324N1.-_inverting_Input_4, C3.0, R7.Pin_0
  N6: LM324N1.Output_4, C3.1, R4.Pin_0, R7.Pin_1
  N7: Composant1.A0, LED1.anode, R4.Pin_1
  N8: C1.0, IR1.Data, R5.Pin_0
  N9: C1.1, R1.Pin_1
  N10: LED2.anode, R6.Pin_0

custom parts:
  LM324N: LM324 LOW POWER QUAD OPERATIONAL AMPLIFIERS
