# Fritzing sketch PROJET Oxymètre Schématique (saved by Fritzing 0.9.3b)
circuit board: 8.46667cm x 5.64444cm
breadboards: 1

parts:
  LM324N1 = LM324N [package=dil14]
  Composant1 = Arduino Uno (Rev3)
  LED1 = LED - 5mm [color="Red (633nm)" package="5 mm [THT]"]
  R1 = Resistor [tolerance=±5% resistance=100 package=THT]
  R2 = Resistor [tolerance=±5% resistance=470 package=THT]
  C1 = Ceramic Capacitor [capacitance="100 nF" package="0603 [SMD, multilayer]"]
  R3 = Resistor [tolerance=±5% resistance=1k package=THT]
  R4 = Resistor [tolerance=±5% resistance=2.2k package=THT]
  R5 = Resistor [tolerance=±5% resistance=22k package=THT]
  R6 = Resistor [tolerance=±5% resistance=1k package=THT]
  C2 = Ceramic Capacitor [capacitance="100 nF" package="0603 [SMD, multilayer]"]
  LED2 = LED - 5mm [color="Infrared (940nm)" package="5 mm [THT]"]
  IR1 = TSOP312.., 314.. [package=THT]

nets (from the schematic view):
  N1: LM324N1.Vcc_+, Composant1.5V, R4.Pin_1, R5.Pin_1
  N2: LM324N1.+_Non-inverting_Input_2, C2.0
  N3: LM324N1.-_Inverting_Input_2, R2.Pin_0, C1.1, R3.Pin_1
  N4: LM324N1.Output_2, R1.Pin_0, R2.Pin_1, C1.0
  GND: LM324N1.Vcc_-, Composant1.GND, LED1.cathode, R3.Pin_0, R6.Pin_1, LED2.cathode, IR1.GND
  N5: Composant1.A0, LED1.anode, R1.Pin_1, IR1.Data
  N6: R4.Pin_0, LED2.anode
  N7: R5.Pin_0, C2.1, IR1.Vs

custom parts:
  LM324N: LM324 LOW POWER QUAD OPERATIONAL AMPLIFIERS
